// Logisim project fib.circ as structural Verilog: 15 circuits, main circuit main
module main (
  input  [63:0] Input
);

  wire clock_1_out, d_ff_1_q, d_ff_2_q, not_1_out, pull_resistor_1_node, Reset_out,
       sixtyfour_bit_equality_checker_1_output, sixtyfour_bit_rca_1_c_out;
  wire [63:0] Reg_A_q, Reg_B_q, Reg_C_q, Reg_R_q, sixtyfour_bit_inc_1_s, sixtyfour_bit_mux_1_y,
       sixtyfour_bit_mux_2_y, sixtyfour_bit_mux_3_y, sixtyfour_bit_rca_1_s;

  Button Reset (.out(Reset_out));
  D_Flip_Flop d_ff_1 (.D(1'b1), .clk(clock_1_out), .Q(d_ff_1_q), .reset(Reset_out));  // open: Qn, preset
  D_Flip_Flop d_ff_2 (.D(d_ff_1_q), .clk(clock_1_out), .Q(d_ff_2_q), .reset(Reset_out));  // open: Qn, preset
  Clock clock_1 (.out(clock_1_out));
  Register #(.width(64)) Reg_R (.D(Input), .en(1'b1), .clk(clock_1_out), .Q(Reg_R_q), .clr(Reset_out));
  Register #(.width(64)) Reg_C (
    .D(sixtyfour_bit_mux_1_y), .en(not_1_out), .clk(clock_1_out), .Q(Reg_C_q), .clr(Reset_out));
  sixtyfour_bit_mux sixtyfour_bit_mux_1 (
    .A({64{1'b0}}), .in_2(sixtyfour_bit_inc_1_s), .in_3(d_ff_2_q), .Y(sixtyfour_bit_mux_1_y));
  not not_1 (not_1_out, sixtyfour_bit_equality_checker_1_output);
  sixtyfour_bit_inc sixtyfour_bit_inc_1 (.A(Reg_C_q), .S(sixtyfour_bit_inc_1_s));
  sixtyfour_bit_equality_checker sixtyfour_bit_equality_checker_1 (
    .in_1(Reg_C_q), .in_2(Reg_R_q), .\output (sixtyfour_bit_equality_checker_1_output));
  sixtyfour_bit_mux sixtyfour_bit_mux_2 (.A({64{1'b0}}), .in_2(Reg_B_q), .in_3(d_ff_2_q), .Y(sixtyfour_bit_mux_2_y));
  sixtyfour_bit_mux sixtyfour_bit_mux_3 (
    .A(64'h1), .in_2(sixtyfour_bit_rca_1_s), .in_3(d_ff_2_q), .Y(sixtyfour_bit_mux_3_y));
  Register #(.width(64)) Reg_A (
    .D(sixtyfour_bit_mux_2_y), .en(not_1_out), .clk(clock_1_out), .Q(Reg_A_q), .clr(Reset_out));
  Register #(.width(64)) Reg_B (
    .D(sixtyfour_bit_mux_3_y), .en(not_1_out), .clk(clock_1_out), .Q(Reg_B_q), .clr(Reset_out));
  LED led_1 (.in(sixtyfour_bit_equality_checker_1_output));
  Pull_Resistor pull_resistor_1 (.node(pull_resistor_1_node));
  Hex_Digit_Display hex_digit_display_1 (.value(Reg_A_q[63:60]));  // open: dp
  Hex_Digit_Display hex_digit_display_2 (.value(Reg_A_q[59:56]));  // open: dp
  Hex_Digit_Display hex_digit_display_3 (.value(Reg_A_q[55:52]));  // open: dp
  sixtyfour_bit_rca sixtyfour_bit_rca_1 (
    .c_in(pull_resistor_1_node), .in_2(Reg_A_q), .in_3(Reg_B_q), .S(sixtyfour_bit_rca_1_s),
    .c_out(sixtyfour_bit_rca_1_c_out));
  // Probe on sixtyfour_bit_rca_1_c_out
  Hex_Digit_Display hex_digit_display_4 (.value(Reg_A_q[51:48]));  // open: dp
  Hex_Digit_Display hex_digit_display_5 (.value(Reg_A_q[47:44]));  // open: dp
  Hex_Digit_Display hex_digit_display_6 (.value(Reg_A_q[43:40]));  // open: dp
  Hex_Digit_Display hex_digit_display_7 (.value(Reg_A_q[39:36]));  // open: dp
  Hex_Digit_Display hex_digit_display_8 (.value(Reg_A_q[35:32]));  // open: dp
  Hex_Digit_Display hex_digit_display_9 (.value(Reg_A_q[31:28]));  // open: dp
  Hex_Digit_Display hex_digit_display_10 (.value(Reg_A_q[27:24]));  // open: dp
  Hex_Digit_Display hex_digit_display_11 (.value(Reg_A_q[23:20]));  // open: dp
  Hex_Digit_Display hex_digit_display_12 (.value(Reg_A_q[19:16]));  // open: dp
  Hex_Digit_Display hex_digit_display_13 (.value(Reg_A_q[15:12]));  // open: dp
  Hex_Digit_Display hex_digit_display_14 (.value(Reg_A_q[11:8]));  // open: dp
  Hex_Digit_Display hex_digit_display_15 (.value(Reg_A_q[7:4]));  // open: dp
  Hex_Digit_Display hex_digit_display_16 (.value(Reg_A_q[3:0]));  // open: dp
endmodule

module one_bit_full_adder (
  input  c_in,
  input  b,
  input  a,
  output s,
  output c_out
);

  wire and_1_out, and_2_out, xor_1_out;

  xor xor_1 (xor_1_out, b, a);
  and and_1 (and_1_out, b, a);
  xor xor_2 (s, xor_1_out, c_in);
  and and_2 (and_2_out, xor_1_out, c_in);
  or or_1 (c_out, and_2_out, and_1_out);
endmodule

module four_bit_rca (
  input  C_in,
  input  [3:0] A,
  input  [3:0] B,
  output [3:0] S,
  output C_out
);

  wire one_bit_full_adder_1_c_out, one_bit_full_adder_2_c_out, one_bit_full_adder_3_c_out;

  one_bit_full_adder one_bit_full_adder_1 (
    .c_in(C_in), .b(A[0]), .a(B[0]), .s(S[0]), .c_out(one_bit_full_adder_1_c_out));
  one_bit_full_adder one_bit_full_adder_2 (
    .c_in(one_bit_full_adder_1_c_out), .b(A[1]), .a(B[1]), .s(S[1]), .c_out(one_bit_full_adder_2_c_out));
  one_bit_full_adder one_bit_full_adder_3 (
    .c_in(one_bit_full_adder_2_c_out), .b(A[2]), .a(B[2]), .s(S[2]), .c_out(one_bit_full_adder_3_c_out));
  one_bit_full_adder one_bit_full_adder_4 (
    .c_in(one_bit_full_adder_3_c_out), .b(A[3]), .a(B[3]), .s(S[3]), .c_out(C_out));
endmodule

module four_bit_inc (
  input  [3:0] A,
  output [3:0] S
);

  wire pull_resistor_1_node;

  Pull_Resistor pull_resistor_1 (.node(pull_resistor_1_node));
  four_bit_rca four_bit_rca_1 (.C_in(pull_resistor_1_node), .A(A), .B(4'b0001), .S(S));  // open: C_out
endmodule

module four_bit_equality_checker (
  input  [3:0] A,
  input  [3:0] B,
  output \output 
);

  wire [3:0] xor_1_out;

  assign xor_1_out = A ^ B;  // XOR_Gate xor_1, 4 bits wide
  nor nor_1 (\output , xor_1_out[0], xor_1_out[1], xor_1_out[2], xor_1_out[3]);
endmodule

module one_bit_mux (
  input  A,
  input  B,
  input  S,
  output Y
);

  wire and_1_out, and_2_out, not_1_out;

  not not_1 (not_1_out, S);
  and and_1 (and_1_out, A, not_1_out);
  and and_2 (and_2_out, S, B);
  or or_1 (Y, and_1_out, and_2_out);
endmodule

module four_bit_mux (
  input  [3:0] A,
  input  [3:0] B,
  input  S,
  output [3:0] Y
);

  one_bit_mux one_bit_mux_1 (.A(A[0]), .B(B[0]), .S(S), .Y(Y[0]));
  one_bit_mux one_bit_mux_2 (.A(A[1]), .B(B[1]), .S(S), .Y(Y[1]));
  one_bit_mux one_bit_mux_3 (.A(A[2]), .B(B[2]), .S(S), .Y(Y[2]));
  one_bit_mux one_bit_mux_4 (.A(A[3]), .B(B[3]), .S(S), .Y(Y[3]));
endmodule

module sixteen_bit_rca (
  input  c_in,
  input  [15:0] A,
  input  [15:0] B,
  output [15:0] S,
  output c_out
);

  wire four_bit_rca_1_c_out, four_bit_rca_2_c_out, four_bit_rca_3_c_out;

  four_bit_rca four_bit_rca_1 (.C_in(c_in), .A(A[3:0]), .B(B[3:0]), .S(S[3:0]), .C_out(four_bit_rca_1_c_out));
  four_bit_rca four_bit_rca_2 (
    .C_in(four_bit_rca_1_c_out), .A(A[7:4]), .B(B[7:4]), .S(S[7:4]), .C_out(four_bit_rca_2_c_out));
  four_bit_rca four_bit_rca_3 (
    .C_in(four_bit_rca_2_c_out), .A(A[11:8]), .B(B[11:8]), .S(S[11:8]), .C_out(four_bit_rca_3_c_out));
  four_bit_rca four_bit_rca_4 (.C_in(four_bit_rca_3_c_out), .A(A[15:12]), .B(B[15:12]), .S(S[15:12]), .C_out(c_out));
endmodule

module sixteen_bit_inc (
  input  [15:0] A,
  output [15:0] S
);

  wire pull_resistor_1_node;

  Pull_Resistor pull_resistor_1 (.node(pull_resistor_1_node));
  sixteen_bit_rca sixteen_bit_rca_1 (.c_in(pull_resistor_1_node), .A(A), .B(16'h1), .S(S));  // open: c_out
endmodule

module sixteen_bit_mux (
  input  [15:0] A,
  input  [15:0] B,
  input  S,
  output [15:0] y
);

  four_bit_mux four_bit_mux_1 (.A(A[3:0]), .B(B[3:0]), .S(S), .Y(y[3:0]));
  four_bit_mux four_bit_mux_2 (.A(A[7:4]), .B(B[7:4]), .S(S), .Y(y[7:4]));
  four_bit_mux four_bit_mux_3 (.A(A[11:8]), .B(B[11:8]), .S(S), .Y(y[11:8]));
  four_bit_mux four_bit_mux_4 (.A(A[15:12]), .B(B[15:12]), .S(S), .Y(y[15:12]));
endmodule

module sixteen_bit_equality_checker (
  input  [15:0] A,
  input  [15:0] B,
  output \output 
);

  wire four_bit_equality_checker_1_output, four_bit_equality_checker_2_output,
       four_bit_equality_checker_3_output, four_bit_equality_checker_4_output;

  four_bit_equality_checker four_bit_equality_checker_1 (
    .A(A[3:0]), .B(B[3:0]), .\output (four_bit_equality_checker_1_output));
  four_bit_equality_checker four_bit_equality_checker_2 (
    .A(A[7:4]), .B(B[7:4]), .\output (four_bit_equality_checker_2_output));
  four_bit_equality_checker four_bit_equality_checker_3 (
    .A(A[11:8]), .B(B[11:8]), .\output (four_bit_equality_checker_3_output));
  four_bit_equality_checker four_bit_equality_checker_4 (
    .A(A[15:12]), .B(B[15:12]), .\output (four_bit_equality_checker_4_output));
  and and_1 (\output , four_bit_equality_checker_1_output, four_bit_equality_checker_2_output, four_bit_equality_checker_3_output, four_bit_equality_checker_4_output);
endmodule

module sixtyfour_bit_rca (
  input  c_in,
  input  [63:0] in_2,
  input  [63:0] in_3,
  output [63:0] S,
  output c_out
);

  wire sixteen_bit_rca_1_c_out, sixteen_bit_rca_2_c_out, sixteen_bit_rca_3_c_out;

  sixteen_bit_rca sixteen_bit_rca_1 (
    .c_in(c_in), .A(in_2[15:0]), .B(in_3[15:0]), .S(S[15:0]), .c_out(sixteen_bit_rca_1_c_out));
  sixteen_bit_rca sixteen_bit_rca_2 (
    .c_in(sixteen_bit_rca_1_c_out), .A(in_2[31:16]), .B(in_3[31:16]), .S(S[31:16]),
    .c_out(sixteen_bit_rca_2_c_out));
  sixteen_bit_rca sixteen_bit_rca_3 (
    .c_in(sixteen_bit_rca_2_c_out), .A(in_2[47:32]), .B(in_3[47:32]), .S(S[47:32]),
    .c_out(sixteen_bit_rca_3_c_out));
  sixteen_bit_rca sixteen_bit_rca_4 (
    .c_in(sixteen_bit_rca_3_c_out), .A(in_2[63:48]), .B(in_3[63:48]), .S(S[63:48]), .c_out(c_out));
endmodule

module sixtyfour_bit_inc (
  input  [63:0] A,
  output [63:0] S
);

  wire pull_resistor_1_node;

  Pull_Resistor pull_resistor_1 (.node(pull_resistor_1_node));
  sixtyfour_bit_rca sixtyfour_bit_rca_1 (.c_in(pull_resistor_1_node), .in_2(A), .in_3(64'h1), .S(S));  // open: c_out
endmodule

module sixtyfour_bit_mux (
  input  [63:0] A,
  input  [63:0] in_2,
  input  in_3,
  output [63:0] Y
);

  sixteen_bit_mux sixteen_bit_mux_1 (.A(A[15:0]), .B(in_2[15:0]), .S(in_3), .y(Y[15:0]));
  sixteen_bit_mux sixteen_bit_mux_2 (.A(A[31:16]), .B(in_2[31:16]), .S(in_3), .y(Y[31:16]));
  sixteen_bit_mux sixteen_bit_mux_3 (.A(A[47:32]), .B(in_2[47:32]), .S(in_3), .y(Y[47:32]));
  sixteen_bit_mux sixteen_bit_mux_4 (.A(A[63:48]), .B(in_2[63:48]), .S(in_3), .y(Y[63:48]));
endmodule

module sixtyfour_bit_equality_checker (
  input  [63:0] in_1,
  input  [63:0] in_2,
  output \output 
);

  wire sixteen_bit_equality_checker_1_output, sixteen_bit_equality_checker_2_output,
       sixteen_bit_equality_checker_3_output, sixteen_bit_equality_checker_4_output;

  sixteen_bit_equality_checker sixteen_bit_equality_checker_1 (
    .A(in_1[15:0]), .B(in_2[15:0]), .\output (sixteen_bit_equality_checker_1_output));
  sixteen_bit_equality_checker sixteen_bit_equality_checker_2 (
    .A(in_1[31:16]), .B(in_2[31:16]), .\output (sixteen_bit_equality_checker_2_output));
  sixteen_bit_equality_checker sixteen_bit_equality_checker_3 (
    .A(in_1[47:32]), .B(in_2[47:32]), .\output (sixteen_bit_equality_checker_3_output));
  sixteen_bit_equality_checker sixteen_bit_equality_checker_4 (
    .A(in_1[63:48]), .B(in_2[63:48]), .\output (sixteen_bit_equality_checker_4_output));
  and and_1 (\output , sixteen_bit_equality_checker_1_output, sixteen_bit_equality_checker_2_output, sixteen_bit_equality_checker_3_output, sixteen_bit_equality_checker_4_output);
endmodule
